# Fritzing sketch schema (saved by Fritzing 1.0.4)

parts:
  Rotary_Encoder = IDUINO Rotary Encoder SE055
  Power_supply_5v_3-10A = HLK-PM01
  part = Adafruit MAX9814 Electret Microphone Amplifier [part_number=MAX9814]
  I2C_OLED_128x64 = OLED 0.96" 128x64 I2C SSD1306 [part_number=SSD1306]
  D1_1N4001-1N4007 = Diode [package=diode-1n4001]
  part_2 = ESP32-38PinWide [part_number=ESP-WROWER-32D]
  U2 = WS2812 RGB LED strip
  C2_470mF = Capacitor Polarized [package=cpol-radial-100uf-25v]
  C1_10mF = Capacitor Polarized [package=cpol-radial-100uf-25v]
  R6 = Resistor [tolerance=±5% power=0.25W resistance=10k package=THT]
  LDR = Photocell (LDR) [power=0.25W dark_resistance_@0.01lx=300kΩ light_resistance_@100lx=400Ω luminance=10lx package=THT]
  SD_card_reader = SD Card Module
  part_3 = Adafruit MAX98357A I2S 3W Class D Amplifier [part_number=MAX98357A]
  SPKR_1-3W_(4-8Ω) = Loudspeaker
  Passive_buzzer = Piezo Speaker
  R7 = Resistor [tolerance=±5% power=0.25W resistance=10k package=THT]
  R1 = Resistor [tolerance=±5% power=0.25W resistance=470 package=THT]

nets:
  GND: Rotary_Encoder.GND, Power_supply_5v_3-10A.-Vo, part.GND, I2C_OLED_128x64.GND, part_2.GPIO11, U2.GND, C2_470mF.-, C1_10mF.-, SD_card_reader.GND, part_3.GND, part_3.GAIN
  VDD: Rotary_Encoder.VDD, part.VDD, I2C_OLED_128x64.VCC, part_2.GPIO10, SD_card_reader.+3.3, Passive_buzzer.pin2, R7.Pin_1
  N1: Rotary_Encoder.SW, part_2.GPIO15
  N2: Rotary_Encoder.DT, part_2.GPIO2
  N3: Rotary_Encoder.CLK, part_2.GPIO4
  N4: Power_supply_5v_3-10A.+Vo, D1_1N4001-1N4007.A, U2.VCC, C2_470mF.+
  N5: part.OUTPUT, part_2.GPIO35
  N6: I2C_OLED_128x64.SCL, part_2.GPIO22
  N7: I2C_OLED_128x64.SCA, part_2.GPIO21
  VIN: D1_1N4001-1N4007.C, part_2.VIN, part_3.VIN
  N8: part_2.3.3, LDR.pin_0
  N9: part_2.EN, C1_10mF.+
  N10: part_2.GPIO34, R6.Pin_1, LDR.pin_1
  N11: part_2.GPIO32, Passive_buzzer.pin1
  N12: part_2.GPIO33, R1.Pin_0
  N13: part_2.GPIO25, part_3.LRCLK
  N14: part_2.GPIO26, part_3.BCLK
  N15: part_2.GPIO27, part_3.DIN
  N16: part_2.GPIO5, SD_card_reader.CS
  N17: part_2.GPIO18, SD_card_reader.SCK
  N18: part_2.GPIO19, SD_card_reader.MISO, R7.Pin_0
  N19: part_2.GPIO23, SD_card_reader.MOSI
  N20: part_2.GND, R6.Pin_0
  N21: U2.DIN, R1.Pin_1
  N22: part_3.VO-, SPKR_1-3W_(4-8Ω).pin1
  N23: part_3.VO+, SPKR_1-3W_(4-8Ω).pin2

custom parts:
  IDUINO Rotary Encoder SE055: https://www.conrad.com/p/iduino-rotary-encoder-1-pcs-se055-1485328
  Adafruit MAX9814 Electret Microphone Amplifier: Add an ear to your project with this well-designed electret microphone amplifier with AGC. This fully assembled and tested board comes with a 20-20KHz electret microphone soldered on. For the amplification, we use the Maxim MAX9814, a specialty chip that is designed for amplifying electret microphones in situations where the loudness of the audio isn't predictable. This fancy microphone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
  ESP32-38PinWide: Generic 38-Pin ESP32 with wide format (only access to one side of pins on a breadboard) based on Stephen Lilley's HiLetgo ESP-WROOM-32 ESP32 ESP-32S Development Board.
  WS2812 RGB LED strip: WS2812 strip
  SD Card Module: SD Card Module Slot Socket Reader For Arduino ARM MCU
  Adafruit MAX98357A I2S 3W Class D Amplifier: Listen to this good news - we now have an all in one digital audio amp breakout board that works incredibly well with the Raspberry Pi! If you're looking for an easy and low cost way to get you digital sound files bumpin' then the MAX08357 I2S Amp Breakout is for you. It takes standard I2S digital audio input and, not only decodes it into analog, but also amplifies it directly into a speaker.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
